# Fritzing sketch Schematic (saved by Fritzing 0.9.10b)
breadboards: 1

parts:
  Arduino_Uno = Arduino Uno (Rev3) - ICSP
  U1 = LCD-16X2 [package=lcd-16x2_noholes]
  I2C = IC, SIP package, 20 pins [chip_label=I2C]
  Photo_Resistor = PHOTOCELL [package=photocell]
  R2 = Resistor [tolerance=±5% power=0.25 resistance=220 package=THT]
  PN532 = IC, SIP package, 4 pins [chip_label=PN532]
  buzzer = Piezo Speaker

nets:
  N1: Arduino_Uno.A0, Photo_Resistor.P$1, R2.Pin_1
  N2: Arduino_Uno.A4/SDA, I2C.pin2, PN532.pin4
  N3: Arduino_Uno.A5/SCL, I2C.pin1, PN532.pin3
  N4: Arduino_Uno.5V, I2C.pin3, Photo_Resistor.P$2, PN532.pin2
  N5: Arduino_Uno.GND, I2C.pin4, PN532.pin1, buzzer.pin2
  N6: Arduino_Uno.D3_PWM, buzzer.pin1
  N7: U1.VSS, I2C.pin20
  N8: U1.VDD, I2C.pin19
  N9: U1.VO, I2C.pin18
  N10: U1.RS, I2C.pin17
  N11: U1.R_W, I2C.pin16
  N12: U1.E, I2C.pin15
  N13: U1.DB0, I2C.pin14
  N14: U1.DB1, I2C.pin13
  N15: U1.DB2, I2C.pin12
  N16: U1.DB3, I2C.pin11
  N17: U1.DB4, I2C.pin10
  N18: U1.DB5, I2C.pin9
  N19: U1.DB6, I2C.pin8
  N20: U1.DB7, I2C.pin7
  N21: U1.A, I2C.pin6
  N22: U1.K, I2C.pin5
